# Fritzing sketch BreadboardSynthSchematic (saved by Fritzing 0.9.3b)
breadboards: 1

parts:
  U1 = 555 Timer [package="SO8 [SMD]"]  # not connected
  R1 = Resistor [tolerance=±5% resistance=100 package=THT]
  R2 = Resistor [tolerance=±5% resistance=100 package=THT]
  R3 = Photocell (LDR) [package=THT]
  S2 = Pushbutton [package="[THT]"]
  C3 = Electrolytic Capacitor [capacitance=2.2µF package="0405 [SMD, electrolytic]"]
  LED1 = LED - 3mm [color="White (6500K)" package="3 mm [THT]"]
  VCC1 = Battery block 9V
  C2 = Electrolytic Capacitor [capacitance=47µF voltage=10V package="200 mil [THT, electrolytic]"]
  J1 = Piezo Speaker

nets:
  N1: R1.Pin_0, R3.pin_1
  N2: R1.Pin_1, C3.+
  N3: R2.Pin_0, C3.-, VCC1.-, J1.pin1
  N4: R2.Pin_1, LED1.cathode
  N5: R3.pin_0, S2.Pin_1, S2.Pin_2, LED1.anode
  N6: S2.Pin_3, S2.Pin_4, VCC1.+
  N7: C2.-, J1.pin2
